// Logisim project base.circ as structural Verilog: 1 circuit, main circuit Teste
module Teste (
);

  wire clock_1_out, j_k_ff_1_q, j_k_ff_2_q, j_k_ff_3_q, or_1_out, or_2_out, or_3_out, or_4_out;

  Clock clock_1 (.out(clock_1_out));
  or or_1 (or_1_out, ~j_k_ff_2_q, j_k_ff_3_q);  // OR_Gate
  or or_2 (or_2_out, j_k_ff_3_q, j_k_ff_1_q);
  or or_3 (or_3_out, ~j_k_ff_1_q, j_k_ff_2_q);  // OR_Gate
  or or_4 (or_4_out, j_k_ff_2_q, j_k_ff_1_q);
  J_K_Flip_Flop j_k_ff_1 (.J(or_1_out), .clk(clock_1_out), .K(1'b1), .Q(j_k_ff_1_q));  // open: Qn, preset, en, reset
  J_K_Flip_Flop j_k_ff_2 (
    .J(j_k_ff_3_q), .clk(clock_1_out), .K(or_2_out), .Q(j_k_ff_2_q));  // open: Qn, preset, en, reset
  J_K_Flip_Flop j_k_ff_3 (
    .J(or_3_out), .clk(clock_1_out), .K(or_4_out), .Q(j_k_ff_3_q));  // open: Qn, preset, en, reset

  // Notes on the sheet:
  //   C
  //   B
  //   A
endmodule
