// Logisim project base.circ as structural Verilog: 1 circuit, main circuit base_2
module base_2 (
);

  wire clock_1_out, j_k_ff_1_q, j_k_ff_2_q;

  Clock clock_1 (.out(clock_1_out));
  J_K_Flip_Flop j_k_ff_1 (.J(1'b1), .clk(clock_1_out), .K(j_k_ff_2_q), .Q(j_k_ff_1_q));  // open: Qn, preset, en, reset
  J_K_Flip_Flop j_k_ff_2 (.J(1'b1), .clk(clock_1_out), .K(j_k_ff_1_q), .Q(j_k_ff_2_q));  // open: Qn, preset, en, reset
  J_K_Flip_Flop j_k_ff_3 (.J(j_k_ff_1_q), .clk(clock_1_out), .K(j_k_ff_1_q));  // open: Q, Qn, preset, en, reset

  // Notes on the sheet:
  //   C
  //   B
  //   A
endmodule
